// Logisim project ALU.circ as structural Verilog
module Selector (
  input  A,
  input  C,
  input  B,
  output S
);

  wire and_1_out, and_2_out, not_1_out;

  not not_1 (not_1_out, C);
  and and_1 (and_1_out, A, not_1_out);
  and and_2 (and_2_out, C, B);
  or or_1 (S, and_1_out, and_2_out);
endmodule

module Half_adder (
  input  A,
  input  B,
  output S,
  output C
);

  wire and_2_out, and_3_out, not_1_out, not_2_out;

  not not_1 (not_1_out, A);
  not not_2 (not_2_out, B);
  and and_1 (C, A, B);
  and and_2 (and_2_out, not_1_out, B);
  and and_3 (and_3_out, A, not_2_out);
  or or_1 (S, and_2_out, and_3_out);
endmodule

module Full_Adder (
  input  A,
  input  B,
  input  Cin,
  output S,
  output Cout
);

  wire and_1_out, and_2_out, and_3_out, and_4_out, and_5_out, and_6_out, and_7_out, and_8_out, and_9_out,
       and_10_out, and_11_out, not_1_out, not_2_out, not_3_out, not_4_out, not_5_out, not_6_out, or_1_out,
       or_3_out, or_4_out;

  not not_1 (not_1_out, A);
  and and_1 (and_1_out, not_1_out, not_2_out);
  not not_2 (not_2_out, B);
  not not_3 (not_3_out, A);
  and and_2 (and_2_out, not_3_out, B);
  not not_4 (not_4_out, Cin);
  and and_3 (and_3_out, A, not_5_out);
  not not_5 (not_5_out, B);
  not not_6 (not_6_out, Cin);
  and and_4 (and_4_out, A, B);
  and and_5 (and_5_out, B, Cin);
  and and_6 (and_6_out, A, Cin);
  and and_7 (and_7_out, and_1_out, Cin);
  and and_8 (and_8_out, and_2_out, not_4_out);
  and and_9 (and_9_out, and_3_out, not_6_out);
  and and_10 (and_10_out, and_4_out, Cin);
  or or_1 (or_1_out, and_5_out, and_6_out);
  or or_2 (Cout, or_1_out, and_11_out);
  and and_11 (and_11_out, A, B);
  or or_3 (or_3_out, and_7_out, and_8_out);
  or or_4 (or_4_out, and_9_out, and_10_out);
  or or_5 (S, or_3_out, or_4_out);
endmodule

module _8bit_adder_sub (
  input  [7:0] A,
  input  [7:0] B,
  input  Sub,
  output Flag,
  output [7:0] S
);

  wire full_adder_2_cout, full_adder_3_cout, full_adder_4_cout, full_adder_5_cout, full_adder_6_cout,
       full_adder_7_cout, full_adder_8_cout, xor_1_out, xor_2_out, xor_3_out, xor_4_out, xor_5_out,
       xor_6_out, xor_7_out, xor_8_out;

  Full_Adder full_adder_1 (.A(A[7]), .B(xor_1_out), .Cin(full_adder_2_cout), .S(S[7]), .Cout(Flag));
  xor xor_1 (xor_1_out, Sub, B[7]);
  Full_Adder full_adder_2 (.A(A[6]), .B(xor_2_out), .Cin(full_adder_3_cout), .S(S[6]), .Cout(full_adder_2_cout));
  xor xor_2 (xor_2_out, Sub, B[6]);
  xor xor_3 (xor_3_out, Sub, B[5]);
  Full_Adder full_adder_3 (.A(A[5]), .B(xor_3_out), .Cin(full_adder_4_cout), .S(S[5]), .Cout(full_adder_3_cout));
  xor xor_4 (xor_4_out, Sub, B[4]);
  xor xor_5 (xor_5_out, Sub, B[3]);
  Full_Adder full_adder_4 (.A(A[4]), .B(xor_4_out), .Cin(full_adder_5_cout), .S(S[4]), .Cout(full_adder_4_cout));
  xor xor_6 (xor_6_out, Sub, B[2]);
  Full_Adder full_adder_5 (.A(A[3]), .B(xor_5_out), .Cin(full_adder_6_cout), .S(S[3]), .Cout(full_adder_5_cout));
  xor xor_7 (xor_7_out, Sub, B[1]);
  Full_Adder full_adder_6 (.A(A[2]), .B(xor_6_out), .Cin(full_adder_7_cout), .S(S[2]), .Cout(full_adder_6_cout));
  Full_Adder full_adder_7 (.A(A[1]), .B(xor_7_out), .Cin(full_adder_8_cout), .S(S[1]), .Cout(full_adder_7_cout));
  xor xor_8 (xor_8_out, Sub, B[0]);
  Full_Adder full_adder_8 (.A(A[0]), .B(xor_8_out), .Cin(Sub), .S(S[0]), .Cout(full_adder_8_cout));
endmodule

module And_8bit (
  input  [7:0] A,
  input  [7:0] B,
  output [7:0] S
);

  and and_1 (S[0], A[0], B[0]);
  and and_2 (S[1], A[1], B[1]);
  and and_3 (S[2], A[2], B[2]);
  and and_4 (S[3], A[3], B[3]);
  and and_5 (S[4], A[4], B[4]);
  and and_6 (S[5], A[5], B[5]);
  and and_7 (S[6], A[6], B[6]);
  and and_8 (S[7], A[7], B[7]);
endmodule

module Or_8bit (
  input  [7:0] A,
  input  [7:0] B,
  output [7:0] S
);

  or or_1 (S[0], A[0], B[0]);
  or or_2 (S[1], A[1], B[1]);
  or or_3 (S[2], A[2], B[2]);
  or or_4 (S[3], A[3], B[3]);
  or or_5 (S[4], A[4], B[4]);
  or or_6 (S[5], A[5], B[5]);
  or or_7 (S[6], A[6], B[6]);
  or or_8 (S[7], A[7], B[7]);
endmodule

module XOR_8bit (
  input  [7:0] A,
  input  [7:0] B,
  output [7:0] S
);

  xor xor_1 (S[0], A[0], B[0]);
  xor xor_2 (S[1], A[1], B[1]);
  xor xor_3 (S[2], A[2], B[2]);
  xor xor_4 (S[3], A[3], B[3]);
  xor xor_5 (S[4], A[4], B[4]);
  xor xor_6 (S[5], A[5], B[5]);
  xor xor_7 (S[6], A[6], B[6]);
  xor xor_8 (S[7], A[7], B[7]);
endmodule

module NOT_8bit (
  input  [7:0] A,
  output [7:0] S
);

  not not_1 (S[7], A[7]);
  not not_2 (S[6], A[6]);
  not not_3 (S[5], A[5]);
  not not_4 (S[3], A[3]);
  not not_5 (S[4], A[4]);
  not not_6 (S[1], A[1]);
  not not_7 (S[2], A[2]);
  not not_8 (S[0], A[0]);
endmodule

module Shift_left_8bit (
  input  [7:0] A,
  output Flag_C,
  output [7:0] S
);


  assign Flag_C = A[7];
  assign S = {A[6:0], 1'b0};
endmodule

module SHR_8bit (
  input  [7:0] A,
  output Flag_C,
  output [7:0] S
);


  assign Flag_C = A[0];
  assign S = {1'b0, A[7:1]};
endmodule

module ALU (
  input  [7:0] A,
  input  [7:0] B,
  input  [2:0] op,
  output Flag_Z,
  output Flag_N,
  output [7:0] Output,
  output Flag_C,
  output Flag_V
);

  wire and_1_out, and_2_out, and_3_out, and_4_out, n8bit_adder_sub_1_flag, n8bit_adder_sub_2_flag, not_1_out,
       not_2_out, not_3_out, or_2_out, shift_left_8bit_1_flag_c, shr_8bit_1_flag_c;
  wire [7:0] and_8bit_1_s, n8bit_adder_sub_1_s, n8bit_adder_sub_2_s, not_8bit_1_s, or_8bit_1_s,
       shift_left_8bit_1_s, shr_8bit_1_s, xor_8bit_1_s;

  not not_1 (not_1_out, B[7]);
  not not_2 (not_2_out, A[7]);
  and and_1 (and_1_out, not_1_out, not_2_out);
  and and_2 (and_2_out, B[7], A[7]);
  not not_3 (not_3_out, Flag_N);
  and and_3 (and_3_out, Flag_N, and_1_out);
  and and_4 (and_4_out, not_3_out, and_2_out);
  _8bit_adder_sub u_8bit_adder_sub_1 (.Sub(1'b0), .A(A), .B(B), .Flag(n8bit_adder_sub_1_flag), .S(n8bit_adder_sub_1_s));
  _8bit_adder_sub u_8bit_adder_sub_2 (.Sub(1'b1), .A(A), .B(B), .Flag(n8bit_adder_sub_2_flag), .S(n8bit_adder_sub_2_s));
  And_8bit and_8bit_1 (.S(and_8bit_1_s), .A(A), .B(B));
  Or_8bit or_8bit_1 (.S(or_8bit_1_s), .A(A), .B(B));
  XOR_8bit xor_8bit_1 (.S(xor_8bit_1_s), .A(A), .B(B));
  NOT_8bit not_8bit_1 (.A(A), .S(not_8bit_1_s));
  Shift_left_8bit shift_left_8bit_1 (.A(A), .Flag_C(shift_left_8bit_1_flag_c), .S(shift_left_8bit_1_s));
  SHR_8bit shr_8bit_1 (.A(A), .S(shr_8bit_1_s), .Flag_C(shr_8bit_1_flag_c));
  Multiplexer #(.select(3), .width(8)) multiplexer_1 (
    .in0(n8bit_adder_sub_1_s), .in1(n8bit_adder_sub_2_s), .in2(and_8bit_1_s), .in3(or_8bit_1_s),
    .in4(xor_8bit_1_s), .in5(not_8bit_1_s), .in6(shift_left_8bit_1_s), .in7(shr_8bit_1_s),
    .out({Flag_N, Output[6:0]}), .sel(op));  // open: en
  or or_1 (Flag_V, and_3_out, and_4_out);
  Multiplexer #(.select(3)) multiplexer_2 (
    .in0(n8bit_adder_sub_1_flag), .in1(n8bit_adder_sub_2_flag), .in2(1'b0), .in3(1'b0), .in4(1'b0),
    .in5(1'b0), .in6(shift_left_8bit_1_flag_c), .in7(shr_8bit_1_flag_c), .out(Flag_C), .sel(op));  // open: en
  or or_2 (or_2_out, Output[0], Output[1], Output[2], Output[3], Output[4], Output[5], Output[6], Flag_N);
  not not_4 (Flag_Z, or_2_out);

  assign Output[7] = Flag_N;
endmodule
