// Logisim project cpu_complet.circ as structural Verilog: 1 circuit, main circuit main
module main (
  input  in_1,
  input  in_2,
  output Z,
  output N,
  output C,
  output V
);

  wire A_IN, ALU_OP0, ALU_OP1, ALU_OP2, ALU_OUT, ALUA_IN, ALUB_IN, and_1_out, and_2_out, and_3_out,
       and_4_out, and_5_out, and_6_out, and_7_out, and_8_out, and_9_out, and_10_out, and_11_out, B_IN, C_t,
       CLOCK_out, double_dabble_1_p3, double_dabble_2_p3, double_dabble_3_p3, F_IN, IR_IN, IR_OUT,
       JMP_ENABLE, JMP_TYPE0, JMP_TYPE1, JMP_TYPE2, MAR_IN, MDR_FROM_RAM, MDR_IN, MDR_OUT, multiplexer_1_out,
       N_t, PC_INC, PC_OUT, RA_OUT, RAM_READ, RAM_WRITE, RB_OUT, RESET_CTR, RESET_PC_out, SP_DEC, SP_INC,
       V_t, Z_t;
  wire [3:0] counter_1_q, double_dabble_1_p6, double_dabble_1_p9, double_dabble_1_p12, double_dabble_2_p6,
       double_dabble_2_p9, double_dabble_2_p12, double_dabble_3_p6, double_dabble_3_p9, double_dabble_3_p12,
       Instruction_Register_q;
  wire [7:0] alu_1_output, BUS, double_dabble_1_p11, double_dabble_2_p11, IR_OUT_FAIBLE, MAR_q, MDR_IN_q,
       MDR_OUT_q, Program_Counter_q, ram_1_data, Register_B_q, TAMPON_A_q, TAMPON_B_q;

  Clock CLOCK (.out(CLOCK_out));
  Controlled_Buffer controlled_buffer_1 (.in(CLOCK_out), .en(in_2));  // open: out
  Counter #(.width(4), .max('hf)) counter_1 (
    .load(1'b0), .D(4'b0000), .count(1'b1), .Q(counter_1_q), .clk(in_1), .clr(RESET_CTR));  // open: carry
  Register u_MDR_IN (.D(BUS), .en(MDR_IN), .Q(MDR_IN_q), .clk(in_1));  // open: clr
  and and_1 (and_1_out, JMP_ENABLE, Z_t);
  and and_2 (and_2_out, JMP_ENABLE, N_t);
  and and_3 (and_3_out, JMP_ENABLE, C_t);
  and and_4 (and_4_out, JMP_ENABLE, V_t);
  Register MAR (.D(BUS), .en(MAR_IN), .Q(MAR_q), .clk(in_1));  // open: clr
  // Probe on {counter_1_q, Instruction_Register_q}
  // Probe on MAR_q
  RAM #(.bus("separate")) ram_1 (
    .addr(MAR_q), .din(MDR_IN_q), .data(ram_1_data), .str(RAM_WRITE), .clk(in_1), .ld(RAM_READ));  // open: sel, clr
  Multiplexer #(.select(3)) multiplexer_1 (
    .in0(JMP_ENABLE), .in1(and_1_out), .in2(and_2_out), .in3(and_3_out), .in4(and_4_out),
    .out(multiplexer_1_out), .sel({3{JMP_TYPE0}}));  // open: in5, in6, in7, en
  // Probe on ram_1_data
  Register Instruction_Register (
    .D(BUS), .en(IR_IN), .Q({Instruction_Register_q, IR_OUT_FAIBLE[3:0]}), .clk(in_1));  // open: clr
  // Probe on {Instruction_Register_q, IR_OUT_FAIBLE[3:0]}
  ROM #(.dataWidth(28)) rom_1 (
    .addr({counter_1_q, Instruction_Register_q}),
    .data({RESET_CTR, SP_DEC, SP_INC, ALU_OP2, ALU_OP1, ALU_OP0, JMP_TYPE2, JMP_TYPE1, JMP_TYPE0, JMP_ENABLE, PC_INC, MDR_FROM_RAM, RAM_WRITE, RAM_READ, F_IN, ALUB_IN, ALUA_IN, B_IN, A_IN, IR_IN, MDR_IN, MAR_IN, IR_OUT, ALU_OUT, MDR_OUT, RB_OUT, RA_OUT, PC_OUT}));  // open: sel
  Register u_MDR_OUT (.D(ram_1_data), .en(MDR_FROM_RAM), .Q(MDR_OUT_q), .clk(in_1));  // open: clr
  Counter Program_Counter (
    .load(multiplexer_1_out), .D(IR_OUT_FAIBLE), .count(PC_INC), .Q(Program_Counter_q), .clk(in_1),
    .clr(RESET_PC_out));  // open: carry
  assign BUS = and_5_out ? MDR_OUT_q : 8'bz;  // Controlled_Buffer controlled_buffer_2
  and and_5 (and_5_out, MDR_OUT, in_1);
  // Probe on BUS
  assign BUS = and_6_out ? IR_OUT_FAIBLE : 8'bz;  // Controlled_Buffer controlled_buffer_3
  and and_6 (and_6_out, IR_OUT, in_1);
  Button RESET_PC (.out(RESET_PC_out));
  assign BUS = PC_OUT ? Program_Counter_q : 8'bz;  // Controlled_Buffer controlled_buffer_4
  // Probe on BUS
  assign BUS = and_7_out ? double_dabble_1_p11 : 8'bz;  // Controlled_Buffer controlled_buffer_5
  and and_7 (and_7_out, RA_OUT, in_1);
  assign BUS = and_8_out ? Register_B_q : 8'bz;  // Controlled_Buffer controlled_buffer_6
  and and_8 (and_8_out, RB_OUT, in_1);
  // double_dabble double_dabble_1: pin names not known; wires that end beside it: double_dabble_1_p11[7], double_dabble_1_p11[6], double_dabble_1_p3, double_dabble_1_p11[5], double_dabble_1_p11[4], double_dabble_1_p6, double_dabble_1_p11[3], double_dabble_1_p11[2], double_dabble_1_p9, double_dabble_1_p11[1], double_dabble_1_p11[0], double_dabble_1_p12
  _7_Segment_Display u_7_segment_display_1 (.g(double_dabble_1_p3));  // open: f, a, b, e, d, c, dp
  Hex_Digit_Display hex_digit_display_1 (.value(double_dabble_1_p6));  // open: dp
  Hex_Digit_Display hex_digit_display_2 (.value(double_dabble_1_p9));  // open: dp
  Register Register_A (.D(BUS), .Q(double_dabble_1_p11), .clk(and_9_out));  // open: en, clr
  and and_9 (and_9_out, in_1, A_IN);
  Hex_Digit_Display hex_digit_display_3 (.value(double_dabble_1_p12));  // open: dp
  assign BUS = and_10_out ? double_dabble_2_p11 : 8'bz;  // Controlled_Buffer controlled_buffer_7
  and and_10 (and_10_out, ALU_OUT, in_1);
  Register TAMPON_A (.D(BUS), .en(ALUA_IN), .Q(TAMPON_A_q), .clk(in_1));  // open: clr
  ALU alu_1 (
    .Flag_Z(Z), .Flag_N(N), .Output(alu_1_output), .Flag_C(C), .Flag_V(V), .A(TAMPON_A_q), .B(TAMPON_B_q),
    .op({ALU_OP2, ALU_OP1, ALU_OP0}));
  // double_dabble double_dabble_2: pin names not known; wires that end beside it: double_dabble_2_p11[7], double_dabble_2_p11[6], double_dabble_2_p3, double_dabble_2_p11[5], double_dabble_2_p11[4], double_dabble_2_p6, double_dabble_2_p11[3], double_dabble_2_p11[2], double_dabble_2_p9, double_dabble_2_p11[1], double_dabble_2_p11[0], double_dabble_2_p12
  _7_Segment_Display u_7_segment_display_2 (.g(double_dabble_2_p3));  // open: f, a, b, e, d, c, dp
  Hex_Digit_Display hex_digit_display_4 (.value(double_dabble_2_p6));  // open: dp
  Register Register_B (.D(BUS), .Q(Register_B_q), .clk(and_11_out));  // open: en, clr
  and and_11 (and_11_out, in_1, B_IN);
  Register R0 (.D(alu_1_output), .Q(double_dabble_2_p11), .clk(in_1));  // open: en, clr
  Hex_Digit_Display hex_digit_display_5 (.value(double_dabble_2_p9));  // open: dp
  Register TAMPON_B (.D(BUS), .en(ALUB_IN), .Q(TAMPON_B_q), .clk(in_1));  // open: clr
  Hex_Digit_Display hex_digit_display_6 (.value(double_dabble_2_p12));  // open: dp
  // double_dabble double_dabble_3: pin names not known; wires that end beside it: Register_B_q[7], Register_B_q[6], double_dabble_3_p3, Register_B_q[5], Register_B_q[4], double_dabble_3_p6, Register_B_q[3], Register_B_q[2], double_dabble_3_p9, Register_B_q[1], Register_B_q[0], double_dabble_3_p12
  _7_Segment_Display u_7_segment_display_3 (.g(double_dabble_3_p3));  // open: f, a, b, e, d, c, dp
  Hex_Digit_Display hex_digit_display_7 (.value(double_dabble_3_p6));  // open: dp
  Hex_Digit_Display hex_digit_display_8 (.value(double_dabble_3_p9));  // open: dp
  Register #(.width(4)) register_1 (.D({V, C, N, Z}), .en(F_IN), .Q({V_t, C_t, N_t, Z_t}), .clk(in_1));  // open: clr
  Hex_Digit_Display hex_digit_display_9 (.value(double_dabble_3_p12));  // open: dp

  // Other names for the same wires on the sheet: CLK = in_1

  // Notes on the sheet:
  //   contents of rom_1 (hex, n*v repeats v):
  //   16*41 16*14080 16*108 16*20000 8000000 60 60 4*802 60 8040020 80c0020 8140020 0 0 8000204 8000220
  //   8000000 0 14080 14080 4*1004 82 9*0 8000208 8000408 8002210 8802210 8402210 8c02210 8008000
  //   When count is 1 and load is 0, increments D by 1
  //   When count is 1 and load is also 1, decrements D by 1
  //   Reset resets the counter to 0
  //   When count is 0 and load is 1, the counter becomes D when clock is up
  //   OP: 0 0 0   -> Add
  //   0 0 1 -> Sub
  //   0 1 0 -> AND
  //   0 11 -> OR
  //   1 0 0 -> XOR
  //   1 0 1 -> NOT
  //   1 1 0 -> SHL
  //   1 1 1 -> SHR
endmodule
