// Logisim project display_divider_by_10.circ as structural Verilog: 3 circuits, main circuit main
module main (
  input  bit_7,
  input  bit_6,
  input  bit_5,
  input  bit_4,
  input  bit_3,
  input  bit_2,
  input  bit_1,
  input  bit_0,
  output Signe,
  output [3:0] Output_2,
  output [3:0] Output_1,
  output [3:0] Output_0
);

  wire [3:0] divider_1_out;
  wire [7:0] multiplexer_1_out, negator_1_out;

  Negator negator_1 (.in({bit_7, bit_6, bit_5, bit_4, bit_3, bit_2, bit_1, bit_0}), .out(negator_1_out));
  // Probe on negator_1_out
  Multiplexer #(.width(8)) multiplexer_1 (
    .in0({bit_7, bit_6, bit_5, bit_4, bit_3, bit_2, bit_1, bit_0}), .in1(negator_1_out),
    .out(multiplexer_1_out), .sel(bit_7));  // open: en
  Divider #(.width(4)) divider_1 (
    .a(multiplexer_1_out[3:0]), .b(4'b1010), .out(divider_1_out), .upper(multiplexer_1_out[7:4]),
    .rem(Output_0));
  Divider #(.width(4)) divider_2 (.a(divider_1_out), .b(4'b1010), .out(Output_2), .rem(Output_1));  // open: upper

  assign Signe = bit_7;
endmodule

module show_divide_ten (
  input  bit_7,
  input  bit_6,
  input  bit_5,
  input  bit_4,
  input  bit_3,
  input  bit_2,
  input  bit_1,
  input  bit_0
);

  wire [3:0] divider_1_out, divider_1_rem, divider_2_out, divider_2_rem;
  wire [7:0] multiplexer_1_out, negator_1_out;

  Negator negator_1 (.in({bit_7, bit_6, bit_5, bit_4, bit_3, bit_2, bit_1, bit_0}), .out(negator_1_out));
  // Probe on negator_1_out
  _7_Segment_Display u_7_segment_display_1 (.g(bit_7));  // open: f, a, b, e, d, c, dp
  Multiplexer #(.width(8)) multiplexer_1 (
    .in0({bit_7, bit_6, bit_5, bit_4, bit_3, bit_2, bit_1, bit_0}), .in1(negator_1_out),
    .out(multiplexer_1_out), .sel(bit_7));  // open: en
  Hex_Digit_Display hex_digit_display_1 (.value(divider_2_out));  // open: dp
  Hex_Digit_Display hex_digit_display_2 (.value(divider_2_rem));  // open: dp
  Hex_Digit_Display hex_digit_display_3 (.value(divider_1_rem));  // open: dp
  Divider #(.width(4)) divider_1 (
    .a(multiplexer_1_out[3:0]), .b(4'b1010), .out(divider_1_out), .upper(multiplexer_1_out[7:4]),
    .rem(divider_1_rem));
  Divider #(.width(4)) divider_2 (
    .a(divider_1_out), .b(4'b1010), .out(divider_2_out), .rem(divider_2_rem));  // open: upper
endmodule

module abstraction_divide_by_ten (
  input  in_1,
  input  in_2,
  input  in_3,
  input  in_4,
  input  in_5,
  input  in_6,
  input  in_7,
  input  in_8
);

  wire main_1_signe;
  wire [3:0] main_1_output_0, main_1_output_1, main_1_output_2;

  _7_Segment_Display u_7_segment_display_1 (.g(main_1_signe));  // open: f, a, b, e, d, c, dp
  main main_1 (
    .bit_7(in_1), .bit_6(in_2), .bit_5(in_3), .bit_4(in_4), .bit_3(in_5), .bit_2(in_6), .bit_1(in_7),
    .bit_0(in_8), .Output_2(main_1_output_2), .Output_1(main_1_output_1), .Output_0(main_1_output_0),
    .Signe(main_1_signe));
  Hex_Digit_Display hex_digit_display_1 (.value(main_1_output_2));  // open: dp
  Hex_Digit_Display hex_digit_display_2 (.value(main_1_output_0));  // open: dp
  Hex_Digit_Display hex_digit_display_3 (.value(main_1_output_1));  // open: dp
endmodule
