// Logisim project display_double_dabble.circ as structural Verilog: 3 circuits, main circuit plus_3_si_supeg_5
module plus_3_si_supeg_5 (
  input  b0,
  input  b2,
  input  b2_2,
  input  b3,
  output S3,
  output S2,
  output S1,
  output S0
);

  wire and_1_out, and_2_out, and_3_out, and_4_out, and_5_out, and_6_out, and_7_out, and_8_out, and_9_out,
       and_10_out, and_11_out, and_12_out, and_13_out, and_14_out, and_15_out, and_16_out, not_1_out,
       not_2_out, not_3_out, not_4_out, not_5_out, not_6_out, not_7_out, not_8_out, not_9_out, not_10_out,
       or_1_out, or_3_out, or_4_out, or_5_out;

  and and_1 (and_1_out, b2_2, b0);
  and and_2 (and_2_out, b2_2, b2);
  not not_1 (not_1_out, b2);
  not not_2 (not_2_out, b3);
  not not_3 (not_3_out, b2_2);
  not not_4 (not_4_out, b3);
  not not_5 (not_5_out, b2_2);
  or or_1 (or_1_out, and_1_out, and_2_out);
  and and_3 (and_3_out, b2_2, not_1_out);
  not not_6 (not_6_out, b0);
  and and_4 (and_4_out, not_2_out, not_3_out);
  not not_7 (not_7_out, b2);
  and and_5 (and_5_out, not_4_out, not_5_out);
  and and_6 (and_6_out, b2_2, b2);
  not not_8 (not_8_out, b0);
  or or_2 (S3, or_1_out, b3);
  and and_7 (and_7_out, and_3_out, not_6_out);
  or or_3 (or_3_out, and_7_out, and_8_out);
  and and_8 (and_8_out, b3, b0);
  and and_9 (and_9_out, b3, b2);
  and and_10 (and_10_out, and_4_out, b2);
  or or_4 (or_4_out, and_10_out, and_11_out);
  and and_11 (and_11_out, b2, b0);
  and and_12 (and_12_out, b3, not_7_out);
  and and_13 (and_13_out, and_12_out, not_9_out);
  not not_9 (not_9_out, b0);
  and and_14 (and_14_out, and_5_out, b0);
  or or_5 (or_5_out, and_14_out, and_15_out);
  and and_15 (and_15_out, and_6_out, not_8_out);
  and and_16 (and_16_out, b3, not_10_out);
  not not_10 (not_10_out, b0);
  or or_6 (S2, or_3_out, and_9_out);
  or or_7 (S1, or_4_out, and_13_out);
  or or_8 (S0, or_5_out, and_16_out);
endmodule

module double_dabble (
  input  E7,
  input  E6,
  input  E5,
  input  E4,
  input  E3,
  input  E2,
  input  E1,
  input  E0,
  output S3,
  output [3:0] S2,
  output [3:0] S1,
  output [3:0] S0
);

  wire plus_3_si_supeg_5_2_s0, plus_3_si_supeg_5_2_s1, plus_3_si_supeg_5_2_s2, plus_3_si_supeg_5_3_s0,
       plus_3_si_supeg_5_3_s1, plus_3_si_supeg_5_3_s2, plus_3_si_supeg_5_3_s3, plus_3_si_supeg_5_5_s0,
       plus_3_si_supeg_5_5_s1, plus_3_si_supeg_5_5_s2, plus_3_si_supeg_5_5_s3, plus_3_si_supeg_5_6_s0,
       plus_3_si_supeg_5_6_s1, plus_3_si_supeg_5_6_s2, plus_3_si_supeg_5_6_s3, plus_3_si_supeg_5_7_s0,
       plus_3_si_supeg_5_7_s1, plus_3_si_supeg_5_7_s2, plus_3_si_supeg_5_7_s3;
  wire [7:0] negator_1_out;
  wire [7:1] multiplexer_1_out;

  plus_3_si_supeg_5 plus_3_si_supeg_5_1 (
    .b0(plus_3_si_supeg_5_5_s3), .b2(plus_3_si_supeg_5_2_s0), .S3(S2[0]), .b2_2(plus_3_si_supeg_5_2_s1),
    .b3(plus_3_si_supeg_5_2_s2), .S2(S1[3]), .S1(S1[2]), .S0(S1[1]));
  plus_3_si_supeg_5 plus_3_si_supeg_5_2 (
    .b0(plus_3_si_supeg_5_6_s3), .b2(plus_3_si_supeg_5_7_s3), .S3(S2[1]), .b2_2(plus_3_si_supeg_5_3_s3),
    .b3(1'b0), .S2(plus_3_si_supeg_5_2_s2), .S1(plus_3_si_supeg_5_2_s1), .S0(plus_3_si_supeg_5_2_s0));
  plus_3_si_supeg_5 plus_3_si_supeg_5_3 (
    .b0(multiplexer_1_out[5]), .b2(multiplexer_1_out[6]), .S3(plus_3_si_supeg_5_3_s3),
    .b2_2(multiplexer_1_out[7]), .b3(1'b0), .S2(plus_3_si_supeg_5_3_s2), .S1(plus_3_si_supeg_5_3_s1),
    .S0(plus_3_si_supeg_5_3_s0));
  plus_3_si_supeg_5 plus_3_si_supeg_5_4 (
    .b0(multiplexer_1_out[1]), .b2(plus_3_si_supeg_5_5_s0), .S3(S1[0]), .b2_2(plus_3_si_supeg_5_5_s1),
    .b3(plus_3_si_supeg_5_5_s2), .S2(S0[3]), .S1(S0[2]), .S0(S0[1]));
  plus_3_si_supeg_5 plus_3_si_supeg_5_5 (
    .b0(multiplexer_1_out[2]), .b2(plus_3_si_supeg_5_6_s0), .S3(plus_3_si_supeg_5_5_s3),
    .b2_2(plus_3_si_supeg_5_6_s1), .b3(plus_3_si_supeg_5_6_s2), .S2(plus_3_si_supeg_5_5_s2),
    .S1(plus_3_si_supeg_5_5_s1), .S0(plus_3_si_supeg_5_5_s0));
  plus_3_si_supeg_5 plus_3_si_supeg_5_6 (
    .b0(multiplexer_1_out[3]), .b2(plus_3_si_supeg_5_7_s0), .S3(plus_3_si_supeg_5_6_s3),
    .b2_2(plus_3_si_supeg_5_7_s1), .b3(plus_3_si_supeg_5_7_s2), .S2(plus_3_si_supeg_5_6_s2),
    .S1(plus_3_si_supeg_5_6_s1), .S0(plus_3_si_supeg_5_6_s0));
  plus_3_si_supeg_5 plus_3_si_supeg_5_7 (
    .b0(multiplexer_1_out[4]), .b2(plus_3_si_supeg_5_3_s0), .S3(plus_3_si_supeg_5_7_s3),
    .b2_2(plus_3_si_supeg_5_3_s1), .b3(plus_3_si_supeg_5_3_s2), .S2(plus_3_si_supeg_5_7_s2),
    .S1(plus_3_si_supeg_5_7_s1), .S0(plus_3_si_supeg_5_7_s0));
  Multiplexer #(.width(8)) multiplexer_1 (
    .in0({E7, E6, E5, E4, E3, E2, E1, E0}), .in1(negator_1_out), .out({multiplexer_1_out, S0[0]}), .sel(E7));  // open: en
  Negator negator_1 (.in({E7, E6, E5, E4, E3, E2, E1, E0}), .out(negator_1_out));

  assign S2[3:2] = 2'b00;
  assign S3 = E7;
endmodule

module show_double_dabble (
  input  in_1,
  input  in_2,
  input  in_3,
  input  in_4,
  input  in_5,
  input  in_6,
  input  in_7,
  input  in_8
);

  wire plus_3_si_supeg_5_2_s0, plus_3_si_supeg_5_2_s1, plus_3_si_supeg_5_2_s2, plus_3_si_supeg_5_3_s0,
       plus_3_si_supeg_5_3_s1, plus_3_si_supeg_5_3_s2, plus_3_si_supeg_5_3_s3, plus_3_si_supeg_5_5_s0,
       plus_3_si_supeg_5_5_s1, plus_3_si_supeg_5_5_s2, plus_3_si_supeg_5_5_s3, plus_3_si_supeg_5_6_s0,
       plus_3_si_supeg_5_6_s1, plus_3_si_supeg_5_6_s2, plus_3_si_supeg_5_6_s3, plus_3_si_supeg_5_7_s0,
       plus_3_si_supeg_5_7_s1, plus_3_si_supeg_5_7_s2, plus_3_si_supeg_5_7_s3;
  wire [1:0] plus_3_si_supeg_5_1_s3;
  wire [3:0] plus_3_si_supeg_5_4_s0, plus_3_si_supeg_5_4_s3;
  wire [7:0] negator_1_out;
  wire [7:1] multiplexer_1_out;

  _7_Segment_Display u_7_segment_display_1 (.g(in_1));  // open: f, a, b, e, d, c, dp
  Hex_Digit_Display hex_digit_display_1 (.value({2'b00, plus_3_si_supeg_5_1_s3}));  // open: dp
  Hex_Digit_Display hex_digit_display_2 (.value(plus_3_si_supeg_5_4_s3));  // open: dp
  plus_3_si_supeg_5 plus_3_si_supeg_5_1 (
    .b0(plus_3_si_supeg_5_5_s3), .b2(plus_3_si_supeg_5_2_s0), .S3(plus_3_si_supeg_5_1_s3[0]),
    .b2_2(plus_3_si_supeg_5_2_s1), .b3(plus_3_si_supeg_5_2_s2), .S2(plus_3_si_supeg_5_4_s3[3]),
    .S1(plus_3_si_supeg_5_4_s3[2]), .S0(plus_3_si_supeg_5_4_s3[1]));
  plus_3_si_supeg_5 plus_3_si_supeg_5_2 (
    .b0(plus_3_si_supeg_5_6_s3), .b2(plus_3_si_supeg_5_7_s3), .S3(plus_3_si_supeg_5_1_s3[1]),
    .b2_2(plus_3_si_supeg_5_3_s3), .b3(1'b0), .S2(plus_3_si_supeg_5_2_s2), .S1(plus_3_si_supeg_5_2_s1),
    .S0(plus_3_si_supeg_5_2_s0));
  plus_3_si_supeg_5 plus_3_si_supeg_5_3 (
    .b0(multiplexer_1_out[5]), .b2(multiplexer_1_out[6]), .S3(plus_3_si_supeg_5_3_s3),
    .b2_2(multiplexer_1_out[7]), .b3(1'b0), .S2(plus_3_si_supeg_5_3_s2), .S1(plus_3_si_supeg_5_3_s1),
    .S0(plus_3_si_supeg_5_3_s0));
  Hex_Digit_Display hex_digit_display_3 (.value(plus_3_si_supeg_5_4_s0));  // open: dp
  plus_3_si_supeg_5 plus_3_si_supeg_5_4 (
    .b0(multiplexer_1_out[1]), .b2(plus_3_si_supeg_5_5_s0), .S3(plus_3_si_supeg_5_4_s3[0]),
    .b2_2(plus_3_si_supeg_5_5_s1), .b3(plus_3_si_supeg_5_5_s2), .S2(plus_3_si_supeg_5_4_s0[3]),
    .S1(plus_3_si_supeg_5_4_s0[2]), .S0(plus_3_si_supeg_5_4_s0[1]));
  plus_3_si_supeg_5 plus_3_si_supeg_5_5 (
    .b0(multiplexer_1_out[2]), .b2(plus_3_si_supeg_5_6_s0), .S3(plus_3_si_supeg_5_5_s3),
    .b2_2(plus_3_si_supeg_5_6_s1), .b3(plus_3_si_supeg_5_6_s2), .S2(plus_3_si_supeg_5_5_s2),
    .S1(plus_3_si_supeg_5_5_s1), .S0(plus_3_si_supeg_5_5_s0));
  plus_3_si_supeg_5 plus_3_si_supeg_5_6 (
    .b0(multiplexer_1_out[3]), .b2(plus_3_si_supeg_5_7_s0), .S3(plus_3_si_supeg_5_6_s3),
    .b2_2(plus_3_si_supeg_5_7_s1), .b3(plus_3_si_supeg_5_7_s2), .S2(plus_3_si_supeg_5_6_s2),
    .S1(plus_3_si_supeg_5_6_s1), .S0(plus_3_si_supeg_5_6_s0));
  plus_3_si_supeg_5 plus_3_si_supeg_5_7 (
    .b0(multiplexer_1_out[4]), .b2(plus_3_si_supeg_5_3_s0), .S3(plus_3_si_supeg_5_7_s3),
    .b2_2(plus_3_si_supeg_5_3_s1), .b3(plus_3_si_supeg_5_3_s2), .S2(plus_3_si_supeg_5_7_s2),
    .S1(plus_3_si_supeg_5_7_s1), .S0(plus_3_si_supeg_5_7_s0));
  Multiplexer #(.width(8)) multiplexer_1 (
    .in0({in_1, in_2, in_3, in_4, in_5, in_6, in_7, in_8}), .in1(negator_1_out),
    .out({multiplexer_1_out, plus_3_si_supeg_5_4_s0[0]}), .sel(in_1));  // open: en
  Negator negator_1 (.in({in_1, in_2, in_3, in_4, in_5, in_6, in_7, in_8}), .out(negator_1_out));
endmodule
